// Logisim project turtle5x5.circ as structural Verilog: 11 circuits, main circuit main
module main (
  output [2:0] out_1,
  output [2:0] out_2,
  output [7:0] NextPC
);

  wire CLOCK, clock_1_out, controle_saut_1_nextpcsel, ctrlUAL, decodeur_instruction_1_oren,
       decodeur_instruction_1_tren, decodeur_instruction_1_xren, isLoad, regW, RESET, StopClock, TR,
       ual_1_cf, ual_1_of, ual_1_sf, ual_1_zf;
  wire [3:0] OP;
  wire [4:0] dplydriver_1_c0, dplydriver_1_c1, dplydriver_1_c2, dplydriver_1_c3, dplydriver_1_c4;
  wire [5:0] a_c_n, banc_registres_1_rj_2, multiplexer_2_out, Ri, ual_1_out;
  wire [7:0] adder_1_out, adder_2_out, bit_extender_1_out, PC_q;
  wire [11:6] ram_1_data;

  Clock clock_1 (.out(clock_1_out));
  Register PC (.D(NextPC), .Q(PC_q), .clk(CLOCK), .clr(RESET));  // open: en
  Button u_RESET (.out(RESET));
  Button CLOCK_2 ();  // open: out
  and and_1 (CLOCK, clock_1_out, ~StopClock);  // AND_Gate
  Adder adder_1 (.a(PC_q), .b(8'h1), .out(adder_1_out));  // open: cin, cout
  assign bit_extender_1_out = {{2{a_c_n[5]}}, a_c_n};  // Bit_Extender bit_extender_1
  RAM #(.dataWidth(16)) ram_1 (.addr(PC_q), .data({OP, ram_1_data, a_c_n}), .clk(CLOCK));  // open: sel, ld, clr
  Adder adder_2 (.a(adder_1_out), .b(bit_extender_1_out), .out(adder_2_out));  // open: cin, cout
  DECODEUR_INSTRUCTION decodeur_instruction_1 (
    .OP(OP), .StopClock(StopClock), .regW(regW), .isLoad(isLoad), .ctrUAL(ctrlUAL),
    .XRen(decodeur_instruction_1_xren), .TRen(decodeur_instruction_1_tren), .ORen(decodeur_instruction_1_oren));
  Multiplexer #(.width(8), .enable("false")) multiplexer_1 (
    .in0(adder_1_out), .in1(adder_2_out), .out(NextPC), .sel(controle_saut_1_nextpcsel));
  BANC_REGISTRES banc_registres_1 (
    .ri(ram_1_data[11:9]), .rj(ram_1_data[8:6]), .CLOCK(CLOCK), .DataIn(multiplexer_2_out), .RegW(regW),
    .Ri_2(Ri), .Rj_2(banc_registres_1_rj_2));
  Multiplexer #(.width(6), .enable("false")) multiplexer_2 (
    .in0(ual_1_out), .in1(a_c_n), .out(multiplexer_2_out), .sel(isLoad));
  UAL ual_1 (
    .A(Ri), .B(banc_registres_1_rj_2), .SEL(ctrlUAL), .ZF(ual_1_zf), .SF(ual_1_sf), .OUT(ual_1_out),
    .CF(ual_1_cf), .OF(ual_1_of));
  DotMatrix #(.matrixrows(5), .dotshape("circle")) dotmatrix_1 (
    .col0(dplydriver_1_c0), .col1(dplydriver_1_c1), .col2(dplydriver_1_c2), .col3(dplydriver_1_c3),
    .col4(dplydriver_1_c4));
  DPLYdriver dplydriver_1 (
    .TRACE(TR), .XR(out_1), .YR(out_2), .CLOCK(CLOCK), .RESET(RESET), .C0(dplydriver_1_c0),
    .C1(dplydriver_1_c1), .C2(dplydriver_1_c2), .C3(dplydriver_1_c3), .C4(dplydriver_1_c4));
  Controle_Registres controle_registres_1 (
    .XYRen(decodeur_instruction_1_xren), .RESET(RESET), .CLOCK(CLOCK), .ORen(decodeur_instruction_1_oren),
    .a_c_n(a_c_n), .TRen(decodeur_instruction_1_tren), .Ri(Ri), .OP(OP), .Xr(out_1), .Yr(out_2), .Tr(TR));
  CONTROLE_SAUT controle_saut_1 (
    .ZF(ual_1_zf), .SF(ual_1_sf), .CF(ual_1_cf), .OF(ual_1_of), .OP(OP), .nextPCsel(controle_saut_1_nextpcsel));

  // Other names for the same wires on the sheet: XR[2:0] = out_1; YR[2:0] = out_2

  // Notes on the sheet:
  //   Processeur Irving
  //   X31I050 - 2017/2018
  //   LE BADEZET Benoît
  //   PLOUHINEC Glenn
  //   Mémoire programme
endmodule

module DPLYdriver (
  input  TRACE,
  input  [2:0] XR,
  input  [2:0] YR,
  input  CLOCK,
  input  RESET,
  output [4:0] C0,
  output [4:0] C1,
  output [4:0] C2,
  output [4:0] C3,
  output [4:0] C4
);

  wire [4:0] decextx_1_out0, decextx_1_out1, decextx_1_out2, decextx_1_out3, decextx_1_out4, decexty_1_spany,
       multiplexer_1_out, multiplexer_2_out, multiplexer_3_out, multiplexer_4_out, multiplexer_5_out, NX0,
       NX1, NX2, NX3, NX4, X0out, X1out, X2out, X3out, X4out;

  DecExtX decextx_1 (
    .IN(XR), .OUT0(decextx_1_out0), .OUT1(decextx_1_out1), .OUT2(decextx_1_out2), .OUT3(decextx_1_out3),
    .OUT4(decextx_1_out4), .CLOCK(CLOCK), .RESET(RESET), .TRACE(TRACE));
  Register #(.width(5)) X0 (.D(C0), .Q(X0out), .clk(CLOCK), .clr(RESET));  // open: en
  Register #(.width(5)) X1 (.D(C1), .Q(X1out), .clk(CLOCK), .clr(RESET));  // open: en
  Register #(.width(5)) X2 (.D(C2), .Q(X2out), .clk(CLOCK), .clr(RESET));  // open: en
  assign NX0 = decextx_1_out0 & decexty_1_spany;  // AND_Gate and_1, 5 bits wide
  assign NX1 = decextx_1_out1 & decexty_1_spany;  // AND_Gate and_2, 5 bits wide
  assign NX2 = decextx_1_out2 & decexty_1_spany;  // AND_Gate and_3, 5 bits wide
  assign NX3 = decextx_1_out3 & decexty_1_spany;  // AND_Gate and_4, 5 bits wide
  assign NX4 = decextx_1_out4 & decexty_1_spany;  // AND_Gate and_5, 5 bits wide
  DecExtY decexty_1 (.YR(YR), .CLOCK(CLOCK), .RESET(RESET), .TRACE(TRACE), .spanY(decexty_1_spany));
  Register #(.width(5)) X3 (.D(C3), .Q(X3out), .clk(CLOCK), .clr(RESET));  // open: en
  Register #(.width(5)) X4 (.D(C4), .Q(X4out), .clk(CLOCK), .clr(RESET));  // open: en
  // Probe on NX0
  // Probe on NX1
  // Probe on NX2
  // Probe on NX3
  // Probe on NX4
  Multiplexer #(.width(5), .enable("false")) multiplexer_1 (
    .in0({5{1'b0}}), .in1(X0out), .out(multiplexer_1_out), .sel(TRACE));
  Multiplexer #(.width(5), .enable("false")) multiplexer_2 (
    .in0({5{1'b0}}), .in1(X1out), .out(multiplexer_2_out), .sel(TRACE));
  Multiplexer #(.width(5), .enable("false")) multiplexer_3 (
    .in0({5{1'b0}}), .in1(X2out), .out(multiplexer_3_out), .sel(TRACE));
  Multiplexer #(.width(5), .enable("false")) multiplexer_4 (
    .in0({5{1'b0}}), .in1(X3out), .out(multiplexer_4_out), .sel(TRACE));
  Multiplexer #(.width(5), .enable("false")) multiplexer_5 (
    .in0({5{1'b0}}), .in1(X4out), .out(multiplexer_5_out), .sel(TRACE));
  assign C0 = multiplexer_1_out | NX0;  // OR_Gate or_1, 5 bits wide
  assign C1 = multiplexer_2_out | NX1;  // OR_Gate or_2, 5 bits wide
  assign C2 = multiplexer_3_out | NX2;  // OR_Gate or_3, 5 bits wide
  assign C3 = multiplexer_4_out | NX3;  // OR_Gate or_4, 5 bits wide
  assign C4 = multiplexer_5_out | NX4;  // OR_Gate or_5, 5 bits wide

  // Other names for the same wires on the sheet: X0in[4:0] = C0; X1in[4:0] = C1; X2in[4:0] = C2; X3in[4:0] = C3;
  //   X4in[4:0] = C4

  // Notes on the sheet:
  //   Pilote d'affichage
  //   Bug connu : le passage de "trace 1" à "trace 0" efface l'écran.
endmodule

module DecExtX (
  input  [2:0] IN,
  input  CLOCK,
  input  RESET,
  input  TRACE,
  output [4:0] OUT0,
  output [4:0] OUT1,
  output [4:0] OUT2,
  output [4:0] OUT3,
  output [4:0] OUT4
);

  wire [2:0] register_1_q;
  wire [4:0] decoder_1_out0, decoder_2_out0, multiplexer_1_out, spanx_1_spanx;

  Decoder #(.select(3), .enable("false")) decoder_1 (
    .out0(decoder_1_out0[0]), .out1(decoder_1_out0[1]), .out2(decoder_1_out0[2]), .out3(decoder_1_out0[3]),
    .out4(decoder_1_out0[4]), .sel(IN));  // open: out5, out6, out7
  Multiplexer #(.width(5), .enable("false")) multiplexer_1 (
    .in0(decoder_1_out0), .in1(decoder_2_out0), .out(multiplexer_1_out), .sel(TRACE));
  Register #(.width(3)) register_1 (.D(IN), .Q(register_1_q), .clk(CLOCK), .clr(RESET));  // open: en
  Decoder #(.select(3), .enable("false")) decoder_2 (
    .out0(decoder_2_out0[0]), .out1(decoder_2_out0[1]), .out2(decoder_2_out0[2]), .out3(decoder_2_out0[3]),
    .out4(decoder_2_out0[4]), .sel(register_1_q));  // open: out5, out6, out7
  spanX spanx_1 (.oldX(multiplexer_1_out), .newX(decoder_1_out0), .spanX(spanx_1_spanx));
  assign OUT0 = {{4{spanx_1_spanx[0]}}, spanx_1_spanx[0]};  // Bit_Extender bit_extender_1
  assign OUT1 = {{4{spanx_1_spanx[1]}}, spanx_1_spanx[1]};  // Bit_Extender bit_extender_2
  assign OUT2 = {{4{spanx_1_spanx[2]}}, spanx_1_spanx[2]};  // Bit_Extender bit_extender_3
  assign OUT3 = {{4{spanx_1_spanx[3]}}, spanx_1_spanx[3]};  // Bit_Extender bit_extender_4
  assign OUT4 = {{4{spanx_1_spanx[4]}}, spanx_1_spanx[4]};  // Bit_Extender bit_extender_5
endmodule

module spanX (
  input  [4:0] oldX,
  input  [4:0] newX,
  output [4:0] spanX
);

  wire comparator_1_gt;
  wire [4:0] dpyspan_1__2x_1, dpyspan_1_not_x_1, dpyspan_2__2x_1, dpyspan_2_not_x_1, multiplexer_1_out,
       multiplexer_2_out;

  DPYspan dpyspan_1 (.x(oldX), ._2x_1(dpyspan_1__2x_1), .not_x_1(dpyspan_1_not_x_1));
  DPYspan dpyspan_2 (.x(newX), ._2x_1(dpyspan_2__2x_1), .not_x_1(dpyspan_2_not_x_1));
  Comparator #(.width(5), .mode("unsigned")) comparator_1 (.a(newX), .b(oldX), .gt(comparator_1_gt));  // open: eq, lt
  Multiplexer #(.width(5), .enable("false")) multiplexer_1 (
    .in0(dpyspan_1__2x_1), .in1(dpyspan_2__2x_1), .out(multiplexer_1_out), .sel(comparator_1_gt));
  Multiplexer #(.width(5), .enable("false")) multiplexer_2 (
    .in0(dpyspan_2_not_x_1), .in1(dpyspan_1_not_x_1), .out(multiplexer_2_out), .sel(comparator_1_gt));
  assign spanX = multiplexer_1_out & multiplexer_2_out;  // AND_Gate and_1, 5 bits wide
endmodule

module DPYspan (
  input  [4:0] x,
  output [4:0] _2x_1,
  output [4:0] not_x_1
);

  wire [4:0] subtractor_1_out;

  Subtractor #(.width(5)) subtractor_1 (.a(x), .b(5'b00001), .out(subtractor_1_out));  // open: bin, bout
  Adder #(.width(5)) adder_1 (.a(x), .b(subtractor_1_out), .out(_2x_1));  // open: cin, cout
  assign not_x_1 = ~subtractor_1_out;  // NOT_Gate not_1, 5 bits wide

  // Notes on the sheet:
  //   Etant donné un nombre binaire de la forme x=2^a (1 seul bit à 1), retourne 2x-1 et not(x-1)
  //   x-1
endmodule

module DecExtY (
  input  [2:0] YR,
  input  CLOCK,
  input  RESET,
  input  TRACE,
  output [4:0] spanY
);

  wire [2:0] register_1_q;
  wire [4:0] decoder_1_out0, decoder_2_out0, multiplexer_1_out;

  Register #(.width(3)) register_1 (.D(YR), .Q(register_1_q), .clk(CLOCK), .clr(RESET));  // open: en
  Decoder #(.select(3), .enable("false")) decoder_1 (
    .out0(decoder_1_out0[0]), .out1(decoder_1_out0[1]), .out2(decoder_1_out0[2]), .out3(decoder_1_out0[3]),
    .out4(decoder_1_out0[4]), .sel(YR));  // open: out5, out6, out7
  Decoder #(.select(3), .enable("false")) decoder_2 (
    .out0(decoder_2_out0[0]), .out1(decoder_2_out0[1]), .out2(decoder_2_out0[2]), .out3(decoder_2_out0[3]),
    .out4(decoder_2_out0[4]), .sel(register_1_q));  // open: out5, out6, out7
  Multiplexer #(.width(5), .enable("false")) multiplexer_1 (
    .in0(decoder_1_out0), .in1(decoder_2_out0), .out(multiplexer_1_out), .sel(TRACE));
  spanX spanx_1 (.oldX(decoder_1_out0), .newX(multiplexer_1_out), .spanX(spanY));
endmodule

module DECODEUR_INSTRUCTION (
  input  [3:0] OP,
  output StopClock,
  output regW,
  output isLoad,
  output ctrUAL,
  output XRen,
  output TRen,
  output ORen
);

  and and_1 (ctrUAL, OP[3], ~OP[2]);  // AND_Gate
  and and_2 (XRen, ~OP[3], ~OP[2], ~OP[1]);  // AND_Gate
  and and_3 (ORen, ~OP[3], ~OP[2], OP[1]);  // AND_Gate
  and and_4 (TRen, ~OP[3], OP[2], OP[1]);  // AND_Gate
  and and_5 (regW, ~OP[3], OP[2], ~OP[1]);  // AND_Gate
  and and_6 (isLoad, ~OP[3], OP[2], ~OP[1], ~OP[0]);  // AND_Gate
  and and_7 (StopClock, OP[3], OP[2], OP[1], OP[0]);

  // Other names for the same wires on the sheet: bit1 = OP[0]; bit2 = OP[1]; bit3 = OP[2]; bit4 = OP[3]

  // Notes on the sheet:
  //   Entrées
  //   Sorties
endmodule

module UAL (
  input  [5:0] A,
  input  [5:0] B,
  input  SEL,
  output CF,
  output SF,
  output ZF,
  output OF,
  output [5:0] OUT
);

  wire xor_1_out, xor_2_out;
  wire [5:0] adder_1_out, B_prime, not_1_out;

  assign not_1_out = ~B;  // NOT_Gate not_1, 6 bits wide
  Adder #(.width(6)) adder_1 (.a(not_1_out), .b(6'b000001), .out(adder_1_out));  // open: cin, cout
  Multiplexer #(.width(6), .enable("false")) multiplexer_1 (.in0(B), .in1(adder_1_out), .out(B_prime), .sel(SEL));
  xor xor_1 (xor_1_out, A[5], OUT[5]);
  xor xor_2 (xor_2_out, OUT[5], B_prime[5]);
  Adder #(.width(6)) adder_2 (.a(A), .b(B_prime), .out(OUT), .cout(CF));  // open: cin
  and and_1 (OF, xor_1_out, xor_2_out);
  and and_2 (ZF, ~OUT[0], ~OUT[1], ~OUT[2], ~OUT[3], ~OUT[4], ~OUT[5]);  // AND_Gate

  assign SF = OUT[5];

  // Other names for the same wires on the sheet: msbA = A[5]; msbB_prime = B_prime[5]; lsbRES = OUT[0];
  //   bit_1 = OUT[1]; bit_2 = OUT[2]; bit_3 = OUT[3]; bit_4 = OUT[4]; msbRES = OUT[5]

  // Notes on the sheet:
  //   Entrées
  //   0: add
  //   1: sub
  //   Sorties
endmodule

module Controle_Registres (
  input  XYRen,
  input  RESET,
  input  TRen,
  input  CLOCK,
  input  ORen,
  input  [5:0] a_c_n,
  input  [3:0] OP,
  input  [5:0] Ri,
  output [2:0] Xr,
  output [2:0] Yr,
  output Tr
);

  wire newTR, XOREn, YOREn;
  wire [1:0] newOR, OR;
  wire [2:0] adder_1_out, adder_2_out, multiplexer_2_out, newXR, newYR, subtractor_1_out, subtractor_2_out;

  and and_1 (XOREn, XYRen, OR[0]);
  and and_2 (YOREn, XYRen, ~OR[0]);  // AND_Gate
  Multiplexer #(.enable("false")) multiplexer_1 (.in0(a_c_n[0]), .in1(Ri[0]), .out(newTR), .sel(OP[0]));
  Register #(.width(3)) u_XR (.D(newXR), .en(XOREn), .Q(Xr), .clk(CLOCK), .clr(RESET));
  Register #(.width(2)) u_OR (.D(newOR), .en(ORen), .Q(OR), .clk(CLOCK), .clr(RESET));
  Register #(.width(1)) u_TR (.D(newTR), .en(TRen), .Q(Tr), .clk(CLOCK), .clr(RESET));
  Multiplexer #(.width(3), .enable("false")) multiplexer_2 (
    .in0(a_c_n[2:0]), .in1(Ri[2:0]), .out(multiplexer_2_out), .sel(OP[0]));
  Register #(.width(3)) u_YR (.D(newYR), .en(YOREn), .Q(Yr), .clk(CLOCK), .clr(RESET));
  LED led_1 (.in(a_c_n[1]));
  LED led_2 (.in(a_c_n[0]));
  Multiplexer #(.width(2), .enable("false")) multiplexer_3 (.in0(a_c_n[1:0]), .in1(Ri[1:0]), .out(newOR), .sel(OP[0]));
  Adder #(.width(3)) adder_1 (.a(Xr), .b(multiplexer_2_out), .out(adder_1_out));  // open: cin, cout
  Subtractor #(.width(3)) subtractor_1 (.a(Xr), .b(multiplexer_2_out), .out(subtractor_1_out));  // open: bin, bout
  Adder #(.width(3)) adder_2 (.a(Yr), .b(multiplexer_2_out), .out(adder_2_out));  // open: cin, cout
  Subtractor #(.width(3)) subtractor_2 (.a(Yr), .b(multiplexer_2_out), .out(subtractor_2_out));  // open: bin, bout
  Multiplexer #(.width(3), .enable("false")) multiplexer_4 (
    .in0(adder_1_out), .in1(subtractor_1_out), .out(newXR), .sel(OR[1]));
  Multiplexer #(.width(3), .enable("false")) multiplexer_5 (
    .in0(adder_2_out), .in1(subtractor_2_out), .out(newYR), .sel(OR[1]));
endmodule

module BANC_REGISTRES (
  input  [2:0] ri,
  input  [2:0] rj,
  input  CLOCK,
  input  [5:0] DataIn,
  input  RegW,
  output [5:0] Ri_2,
  output [5:0] Rj_2
);

  wire c1, c2, c3, c4, c5, c6, c7, c8;
  wire [2:0] not_1_out;
  wire [5:0] r1, r2, r3, r4, r5, r6, r7, r8;

  Demultiplexer #(.select(3), .enable("false")) demultiplexer_1 (
    .out0(c8), .out1(c7), .out2(c6), .out3(c5), .out4(c4), .out5(c3), .out6(c2), .out7(c1), .in(RegW),
    .sel(not_1_out));
  assign not_1_out = ~ri;  // NOT_Gate not_1, 3 bits wide
  Multiplexer #(.select(3), .width(6), .enable("false")) multiplexer_1 (
    .in0(r1), .in1(r2), .in2(r3), .in3(r4), .in4(r5), .in5(r6), .in6(r7), .in7(r8), .out(Rj_2), .sel(rj));
  Register #(.width(6)) register_1 (.D(DataIn), .en(c1), .Q(r1), .clk(CLOCK));  // open: clr
  Register #(.width(6)) register_2 (.D(DataIn), .en(c2), .Q(r2), .clk(CLOCK));  // open: clr
  Register #(.width(6)) register_3 (.D(DataIn), .en(c3), .Q(r3), .clk(CLOCK));  // open: clr
  Register #(.width(6)) register_4 (.D(DataIn), .en(c4), .Q(r4), .clk(CLOCK));  // open: clr
  Register #(.width(6)) register_5 (.D(DataIn), .en(c5), .Q(r5), .clk(CLOCK));  // open: clr
  Multiplexer #(.select(3), .width(6), .enable("false")) multiplexer_2 (
    .in0(r1), .in1(r2), .in2(r3), .in3(r4), .in4(r5), .in5(r6), .in6(r7), .in7(r8), .out(Ri_2), .sel(ri));
  Register #(.width(6)) register_6 (.D(DataIn), .en(c6), .Q(r6), .clk(CLOCK));  // open: clr
  Register #(.width(6)) register_7 (.D(DataIn), .en(c8), .Q(r8), .clk(CLOCK));  // open: clr
  Register #(.width(6)) register_8 (.D(DataIn), .en(c7), .Q(r7), .clk(CLOCK));  // open: clr

  // Other names for the same wires on the sheet: Ri_t[5:0] = Ri_2; Rj_t[5:0] = Rj_2

  // Notes on the sheet:
  //   Entrées
  //   Sorties
endmodule

module CONTROLE_SAUT (
  input  ZF,
  input  SF,
  input  CF,
  input  OF,
  input  [3:0] OP,
  output nextPCsel
);

  wire and_1_out, and_2_out, and_3_out, and_4_out, and_5_out, and_6_out, and_7_out, Cond, or_2_out;

  and and_1 (and_1_out, ~CF, SF, ~ZF);  // AND_Gate
  and and_2 (and_2_out, ~CF, ~ZF, ~OF);  // AND_Gate
  and and_3 (and_3_out, CF, ~SF, ~ZF);  // AND_Gate
  or or_1 (Cond, and_1_out, and_2_out, and_3_out);
  or or_2 (or_2_out, ZF, Cond);
  and and_4 (and_4_out, OP[3], ~OP[2], ~OP[1], ~OP[0], ZF);  // AND_Gate
  and and_5 (and_5_out, OP[3], ~OP[2], ~OP[1], OP[0], ~ZF);  // AND_Gate
  and and_6 (and_6_out, OP[3], ~OP[2], OP[1], ~OP[0], or_2_out);  // AND_Gate
  and and_7 (and_7_out, OP[3], ~OP[2], OP[1], OP[0], Cond);  // AND_Gate
  or or_3 (nextPCsel, and_4_out, and_5_out, and_6_out, and_7_out);

  // Other names for the same wires on the sheet: b0 = OP[0]; b1 = OP[1]; b2 = OP[2]; b3 = OP[3]

  // Notes on the sheet:
  //   Entrées
  //   Sorties
endmodule
